// Logisim project Tic_Tac_Toe.circ as structural Verilog
module TTTC (
  input  [1:0] hin,
  input  [1:0] vin,
  input  btn,
  output hout,
  output [3:0] L0,
  output [3:0] L1,
  output [3:0] L2,
  output [3:0] L3,
  output vout
);

  wire and_1_out;
  wire [1:0] register_1_q;

  and and_1 (and_1_out, vin[1], hin[1]);
  Register #(.width(2)) register_1 (.D({vin[0], hin[0]}), .en(1'b1), .Q(register_1_q), .clk(and_1_out));  // open: clr
  ROM #(.addrWidth(2), .dataWidth(16)) rom_1 (.addr(register_1_q), .data({L3, L2, L1, L0}));  // open: sel
  Transistor #(.\type ("n"), .gate("br")) transistor_1 (.in(1'b0), .out(hout), .gate(btn));

  assign vout = hout;

  // Notes on the sheet:
  //   contents of rom_1 (hex, n*v repeats v):
  //   0 6996 9249 1010
endmodule

module GSDD (
  input  [1:0] score,
  input  clock,
  output win,
  output lose,
  output draw
);

  wire not_1_out, undriven;
  wire [1:0] register_1_q;

  Register #(.width(2)) register_1 (.D(score), .en(1'b1), .Q(register_1_q), .clk(clock));  // open: clr
  not not_1 (not_1_out, register_1_q[1]);
  and and_1 (win, register_1_q[0], not_1_out);
  xnor xnor_1 (lose, register_1_q[0], register_1_q[1]);
  and and_2 (draw, register_1_q[0], register_1_q[1]);
  Demultiplexer demultiplexer_1 (.in(undriven));  // open: out0, out1, sel, en
endmodule
